# Fritzing sketch airspring (saved by Fritzing 0.9.3b)
circuit board: 6.88566cm x 5.36311cm
breadboards: 1

parts:
  S1 = Pushbutton [package=THT]
  R1 = Resistor [tolerance=±5% resistance=10k package=THT]
  Arduino1 = Arduino Uno (Rev3)
  Grove1 = Grove OLED 128x96
  U1 = 4-Channel 5v Relay Shield [package=relay-4ch5v10a]
  S2 = Pushbutton [package=THT]
  R2 = Resistor [tolerance=±5% resistance=10k package=THT]
  S3 = Pushbutton [package=THT]
  R3 = Resistor [tolerance=±5% resistance=10k package=THT]
  U2 = RELAY [package=OJ]

nets:
  N1: S1.leg0, R1.Pin_0, Arduino1.D2
  VCC: S1.leg1, Arduino1.5V, Grove1.VCC, U1.VCC, S2.leg1, S3.leg1
  GND: R1.Pin_1, Arduino1.GND, Grove1.GND, U1.GND, R2.Pin_1, R3.Pin_1
  N2: Arduino1.A4/SDA, Grove1.SDA
  N3: Arduino1.A5/SCL, Grove1.SCL
  N4: Arduino1.D8, U1.IN3
  N5: Arduino1.D9_PWM, U1.IN4
  N6: Arduino1.D3_PWM, S2.leg0, R2.Pin_0
  N7: Arduino1.D4, S3.leg0, R3.Pin_0
  N8: Arduino1.D6_PWM, U1.IN1
  N9: Arduino1.D7, U1.IN2
  N10: U2.COIL2, U2.COIL1

custom parts:
  4-Channel 5v Relay Shield: 4 Channel 5v Relay Shield w. 2x SPD-06VDC-SD-C

// code stored in the sketch: Button.ino
/*
  Button
 
 Turns on and off a light emitting diode(LED) connected to digital  
 pin 13, when pressing a pushbutton attached to pin 2. 
 
 
 The circuit:
 * LED attached from pin 13 to ground 
 * pushbutton attached to pin 2 from +5V
 * 10K resistor attached to pin 2 from ground
 
 * Note: on most Arduinos there is already an LED on the board
 attached to pin 13.
 
 
 created 2005
 by DojoDave <http://www.0j0.org>
 modified 30 Aug 2011
 by Tom Igoe
 
 This example code is in the public domain.
 
 http://www.arduino.cc/en/Tutorial/Button
 */

// constants won't change. They're used here to 
// set pin numbers:
const int buttonPin = 2;     // the number of the pushbutton pin
const int ledPin =  13;      // the number of the LED pin

// variables will change:
int buttonState = 0;         // variable for reading the pushbutton status

void setup() {
  // initialize the LED pin as an output:
  pinMode(ledPin, OUTPUT);      
  // initialize the pushbutton pin as an input:
  pinMode(buttonPin, INPUT);     
}

void loop(){
  // read the state of the pushbutton value:
  buttonState = digitalRead(buttonPin);

  // check if the pushbutton is pressed.
  // if it is, the buttonState is HIGH:
  if (buttonState == HIGH) {     
    // turn LED on:    
    digitalWrite(ledPin, HIGH);  
  } 
  else {
    // turn LED off:
    digitalWrite(ledPin, LOW); 
  }
}
